# Fritzing sketch VGAX_pong_wiring (saved by Fritzing 0.9.3b)

parts:
  Composant1 = Arduino Uno (Rev3)
  R7 = Resistor [tolerance=±5% resistance=470 package=THT]
  R8 = Resistor [tolerance=±5% resistance=68 package=THT]
  R3 = Resistor [tolerance=±5% resistance=470 package=THT]
  R4 = Resistor [tolerance=±5% resistance=68 package=THT]
  R5 = Rotary Potentiometer (Small) [maximum_resistance=100kΩ package=THT]
  R6 = Rotary Potentiometer (Small) [maximum_resistance=100kΩ package=THT]
  VGA1 = DE15 VGA Connector
  R9 = Resistor [tolerance=±5% resistance=470 package=THT]

nets:
  N1: Composant1.A1, R5.wiper
  N2: Composant1.A2, R6.wiper
  N3: Composant1.D9_PWM, R8.Pin_0
  N4: Composant1.GND, R5.leg1, R6.leg1, VGA1.pin_5, VGA1.pin_6, VGA1.pin_7, VGA1.pin_8, VGA1.pin_10
  N5: Composant1.D3_PWM, R4.Pin_0
  N6: Composant1.D6_PWM, R3.Pin_0
  N7: Composant1.D7, R9.Pin_0
  N8: Composant1.5V, R5.leg2, R6.leg2
  N9: R7.Pin_1, VGA1.pin_1
  N10: R8.Pin_1, VGA1.pin_14
  N11: R3.Pin_1, VGA1.pin_2, VGA1.pin_3, R9.Pin_1
  N12: R4.Pin_1, VGA1.pin_13

custom parts:
  DE15 VGA Connector: A VGA connector
